# Fritzing sketch v0-0-1 (saved by Fritzing 1.0.6)

parts:
  A1 = Esp32-c3 super mini
  R2 = 12mm Trimmer Potentiometer (Large) [maximum_resistance=10kΩ knob_status=50% power=0.5W package=THT]
  R3 = 12mm Trimmer Potentiometer (Large) [maximum_resistance=10kΩ knob_status=50% power=0.5W package=THT]
  R4 = 12mm Trimmer Potentiometer (Large) [maximum_resistance=10kΩ knob_status=50% power=0.5W package=THT]

nets:
  N1: A1.Pin_9, R4.wiper
  N2: A1.Pin_10, R3.wiper
  N3: A1.Pin_11, R2.wiper
  N4: A1.Pin_14, R2.leg2, R3.leg2, R4.leg2
  N5: A1.Pin_15, R2.leg1, R3.leg1, R4.leg1

custom parts:
  Esp32-c3 super mini: ESP32-C3 Development Board ESP32 SuperMini Development Board ESP32 Development Board WiFi Bluetooth.
