# Fritzing sketch v0.1.0 (saved by Fritzing 1.0.6)
breadboards: 1

parts:
  R1 = Basic Flex Resistor
  R2 = Basic Flex Resistor
  R3 = Basic Flex Resistor
  A1 = Esp32-c3 super mini
  R4 = Resistor [tolerance=±5% resistance=4.7k package="0603 [SMD]"]
  R5 = Resistor [tolerance=±5% resistance=4.7k package="0603 [SMD]"]
  R6 = Resistor [tolerance=±5% resistance=4.7k package="0603 [SMD]"]
  Componente1 = InvenSense MPU6050

nets:
  N1: R1.Pin_1, A1.Pin_9, R6.Pin_1
  N2: R1.Pin_2, R2.Pin_2, R3.Pin_2, A1.Pin_14, Componente1.VCC
  N3: R2.Pin_1, A1.Pin_10, R5.Pin_1
  N4: R3.Pin_1, A1.Pin_11, R4.Pin_1
  N5: A1.Pin_4, Componente1.SDA
  N6: A1.Pin_5, Componente1.SCL
  N7: A1.Pin_15, R4.Pin_0, R5.Pin_0, R6.Pin_0, Componente1.GND

custom parts:
  Esp32-c3 super mini: ESP32-C3 Development Board ESP32 SuperMini Development Board ESP32 Development Board WiFi Bluetooth.
