# Fritzing sketch v1-0-0 (saved by Fritzing 1.0.6)
breadboards: 1

parts:
  R1 = Basic Flex Resistor
  R2 = Basic Flex Resistor
  R3 = Basic Flex Resistor
  A1 = Esp32-c3 super mini
  R4 = Resistor [tolerance=±5% resistance=4.7k package="0603 [SMD]"]
  R5 = Resistor [tolerance=±5% resistance=4.7k package="0603 [SMD]"]
  R6 = Resistor [tolerance=±5% resistance=4.7k package="0603 [SMD]"]
  Componente1 = InvenSense MPU6050
  SP1 = SPEAKER [package=pcb_mount_speaker]
  Componente2 = Adafruit MAX98357A I2S 3W Class D Amplifier [part_number="Adafruit #3006"]

nets:
  N1: R1.Pin_1, A1.Pin_9, R6.Pin_1
  N2: R1.Pin_2, R2.Pin_2, R3.Pin_2, A1.Pin_14, Componente1.VCC, Componente2.SD_MODE
  N3: R2.Pin_1, A1.Pin_10, R5.Pin_1
  N4: R3.Pin_1, A1.Pin_11, R4.Pin_1
  N5: A1.Pin_1, Componente2.BCLK
  N6: A1.Pin_2, Componente2.LRCLK
  N7: A1.Pin_3, Componente2.DIN
  N8: A1.Pin_4, Componente1.SDA
  N9: A1.Pin_5, Componente1.SCL
  GND: A1.Pin_15, R4.Pin_0, R5.Pin_0, R6.Pin_0, Componente1.GND, Componente2.GND, Componente2.GAIN
  N10: A1.Pin_16, Componente2.VIN
  N11: SP1.+, Componente2.VO-
  N12: SP1.-, Componente2.VO+

custom parts:
  Esp32-c3 super mini: ESP32-C3 Development Board ESP32 SuperMini Development Board ESP32 Development Board WiFi Bluetooth.
  Adafruit MAX98357A I2S 3W Class D Amplifier: Listen to this good news - we now have an all in one digital audio amp breakout board that works incredibly well with the Raspberry Pi! If you're looking for an easy and low cost way to get you digital sound files bumpin' then the MAX08357 I2S Amp Breakout is for you. It takes standard I2S digital audio input and, not only decodes it into analog, but also amplifies it directly into a speaker.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
